# Fritzing sketch Fritzing (saved by Fritzing 0.9.3b)
breadboards: 1

parts:
  OLED_I2C1 = OLED 128x64 I2C Monochrome Display
  Part1 = Arduino Uno (Rev3)
  ZS-042_RTC1 = ZS-042 RTC Module  # not connected

nets:
  N1: OLED_I2C1.SDA, Part1.A5/SCL
  N2: OLED_I2C1.SCK, Part1.A4/SDA
  VDD: OLED_I2C1.VDD, Part1.5V
  GND: OLED_I2C1.GND, Part1.GND
